# Fritzing sketch meteo_schema (saved by Fritzing 0.9.3b)

parts:
  U3 = ESP8266 NodeMCU LoLin module
  M1 = BMP280
  DHT2 = DHT11 Humitidy and Temperature Sensor (3 pins)

nets:
  N1: U3.D1, M1.SCL
  N2: U3.D2, M1.SDA
  N3: U3.D4, DHT2.Plus
  3V3: U3.3V3, M1.VIN, DHT2.Signal
  GND: U3.GND, M1.GND, DHT2.Gnd

custom parts:
  ESP8266 NodeMCU LoLin module: ESP8266 based NodeMCU
  BMP280: Temperature Humidity Barometric presure Sensor, I2C
  DHT11 Humitidy and Temperature Sensor (3 pins): DHT11 Humidity and Temperature Sensor (3 pins).
